// Logisim project 数字逻辑大作业_20020203王思哲.circ as structural Verilog: 14 circuits, main circuit 异或门
// 20020203
module \大作业逻辑图  (
  input  [3:0] \ＩＮ ,
  input  [1:0] S,
  output [3:0] \ＯＵＴ ,
  output FLAG
);

  wire decoder_1_out5, decoder_1_out6, decoder_1_out7, decoder_1_out8, decoder_1_out9, decoder_1_out10,
       decoder_1_out11, decoder_1_out12, decoder_1_out13, decoder_1_out14, decoder_1_out15, not_1_out,
       or_2_out;
  wire [2:0] xor_1_out;
  wire [3:0] adder_1_out, adder_2_out, multiplexer_1_out, multiplexer_2_out;

  Decoder #(.select(4), .enable("false")) decoder_1 (
    .out5(decoder_1_out5), .out6(decoder_1_out6), .out7(decoder_1_out7), .out8(decoder_1_out8),
    .out9(decoder_1_out9), .out10(decoder_1_out10), .out11(decoder_1_out11), .out12(decoder_1_out12),
    .out13(decoder_1_out13), .out14(decoder_1_out14), .out15(decoder_1_out15), .sel(\ＩＮ ));  // open: out0, out1, out2, out3, out4
  or or_1 (FLAG, decoder_1_out10, decoder_1_out11, decoder_1_out12, decoder_1_out13, decoder_1_out14, decoder_1_out15);
  Adder #(.width(4)) adder_1 (.a(\ＩＮ ), .b(4'b0011), .out(adder_1_out));  // open: cin, cout
  Multiplexer #(.width(4), .enable("false")) multiplexer_1 (
    .in0(4'b0000), .in1(4'b0110), .out(multiplexer_1_out), .sel(or_2_out));
  or or_2 (or_2_out, decoder_1_out5, decoder_1_out6, decoder_1_out7, decoder_1_out8, decoder_1_out9);
  Adder #(.width(4)) adder_2 (.a(\ＩＮ ), .b(multiplexer_1_out), .out(adder_2_out));  // open: cin, cout
  not not_1 (not_1_out, FLAG);
  xor xor_1 (xor_1_out[0], \ＩＮ [0], \ＩＮ [1]);
  xor xor_2 (xor_1_out[1], \ＩＮ [1], \ＩＮ [2]);
  xor xor_3 (xor_1_out[2], \ＩＮ [2], \ＩＮ [3]);
  Multiplexer #(.width(4), .enable("false")) multiplexer_2 (
    .in0({\ＩＮ [3], xor_1_out}), .in1(4'b1000), .out(multiplexer_2_out), .sel(decoder_1_out9));
  Multiplexer #(.select(2), .width(4), .disabled(0)) multiplexer_3 (
    .in0(adder_1_out), .in1(adder_2_out), .in2(multiplexer_2_out), .in3(4'b0000), .out(\ＯＵＴ ), .sel(S),
    .en(not_1_out));
endmodule

module \应用测试  (
  input  [3:0] \ＡＢＣＤ ,
  input  [1:0] \ＳＥＬ ,
  output [3:0] \ＯＵＴ３_０ ,
  output \ＦＬＡＧ 
);

  \大作业逻辑图  \u_大作业逻辑图_1  (.\ＩＮ (\ＡＢＣＤ ), .S(\ＳＥＬ ), .\ＯＵＴ (\ＯＵＴ３_０ ), .FLAG(\ＦＬＡＧ ));
endmodule

module tt (
  input  [7:0] in_1,
  input  in_2,
  input  in_3,
  input  in_4,
  input  in_5,
  input  [1:0] in_6,
  input  in_7,
  input  [2:0] in_8,
  input  in_9,
  input  in_10,
  input  in_11,
  input  in_12,
  input  in_13,
  input  in_14,
  input  in_15,
  input  [7:0] in_16,
  input  in_17,
  input  in_18,
  input  [7:0] in_19,
  input  in_20,
  input  in_21,
  input  in_22,
  output out_23,
  output out_24,
  output out_25,
  output [2:0] out_26,
  output out_27,
  output [15:0] out_28,
  output out_29,
  output [7:0] out_30,
  output [2:0] out_31,
  output [7:0] out_32,
  output out_33
);

  BitSelector bitselector_1 (.in(in_1), .out(out_25), .sel(in_8));
  D_Flip_Flop d_ff_1 ();  // open: clk, D, Q, Qn, preset, en, reset
  Multiplier multiplier_1 ();  // open: a, b, out, cin, cout
  Register register_1 (.D(in_16), .en(in_20), .Q(out_32), .clk(in_21), .clr(in_22));
  Priority_Encoder priority_encoder_1 (
    .in0(in_2), .in1(in_4), .in2(in_5), .in3(in_7), .in4(in_9), .in5(in_10), .in6(in_11), .in7(in_12),
    .out(out_26), .en_in(in_13), .gs(out_27), .en_out(out_24));
  Negator negator_1 (.in(in_16), .out(out_30));
  BitFinder bitfinder_1 (.in(in_19), .index(out_31), .found(out_33));
  Decoder #(.select(2)) decoder_1 (.out0(out_23), .sel(in_6), .en(in_3));  // open: out1, out2, out3
  assign out_28 = {{8{1'b0}}, in_16};  // Bit_Extender bit_extender_1
  Multiplexer multiplexer_1 (.in0(in_18), .in1(in_17), .out(out_29), .sel(in_14), .en(in_15));
endmodule

module \全加器  (
  input  \被加数 ,
  input  \加数 ,
  input  \低位向本位进位 ,
  output \本位和 ,
  output \本位向高位进位 
);

  wire and_1_out, and_2_out, and_3_out, \异或门_1_out_3 ;

  \异或门  \u_异或门_1  (.in_1(\被加数 ), .in_2(\加数 ), .out_3(\异或门_1_out_3 ));
  and and_1 (and_1_out, \被加数 , \加数 );
  and and_2 (and_2_out, \被加数 , \低位向本位进位 );
  and and_3 (and_3_out, \加数 , \低位向本位进位 );
  \异或门  \u_异或门_2  (.in_1(\异或门_1_out_3 ), .in_2(\低位向本位进位 ), .out_3(\本位和 ));
  or or_1 (\本位向高位进位 , and_1_out, and_2_out, and_3_out);
endmodule

module \异或门  (
  input  in_1,
  input  in_2,
  output out_3
);

  wire and_1_out, and_2_out, not_1_out, not_2_out;

  not not_1 (not_1_out, in_1);
  not not_2 (not_2_out, in_2);
  and and_1 (and_1_out, not_1_out, in_2);
  and and_2 (and_2_out, not_2_out, in_1);
  or or_1 (out_3, and_1_out, and_2_out);
endmodule

module \_4位全加器  (
  input  in_1,
  input  in_2,
  input  in_3,
  input  in_4,
  input  in_5,
  input  in_6,
  input  in_7,
  input  in_8,
  input  in_9,
  output out_10,
  output out_11,
  output out_12,
  output out_13,
  output out_14
);

  wire \全加器_2_本位向高位进位 , \全加器_3_本位向高位进位 , \全加器_4_本位向高位进位 ;

  \全加器  \u_全加器_1  (.\被加数 (in_1), .\加数 (in_2), .\低位向本位进位 (\全加器_2_本位向高位进位 ), .\本位和 (out_11), .\本位向高位进位 (out_10));
  \全加器  \u_全加器_2  (.\被加数 (in_3), .\加数 (in_4), .\低位向本位进位 (\全加器_3_本位向高位进位 ), .\本位和 (out_12), .\本位向高位进位 (\全加器_2_本位向高位进位 ));
  \全加器  \u_全加器_3  (.\被加数 (in_5), .\加数 (in_6), .\低位向本位进位 (\全加器_4_本位向高位进位 ), .\本位和 (out_13), .\本位向高位进位 (\全加器_3_本位向高位进位 ));
  \全加器  \u_全加器_4  (.\被加数 (in_7), .\加数 (in_8), .\低位向本位进位 (in_9), .\本位和 (out_14), .\本位向高位进位 (\全加器_4_本位向高位进位 ));
endmodule

module \_16位全加器  (
  input  in_1,
  input  in_2,
  input  in_3,
  input  in_4,
  input  in_5,
  input  in_6,
  input  in_7,
  input  in_8,
  input  in_9,
  input  in_10,
  input  in_11,
  input  in_12,
  input  in_13,
  input  in_14,
  input  in_15,
  input  in_16,
  input  in_17,
  input  in_18,
  input  in_19,
  input  in_20,
  input  in_21,
  input  in_22,
  input  in_23,
  input  in_24,
  input  in_25,
  input  in_26,
  input  in_27,
  input  in_28,
  input  in_29,
  input  in_30,
  input  in_31,
  input  in_32,
  input  in_33,
  output out_34,
  output out_35,
  output out_36,
  output out_37,
  output out_38,
  output out_39,
  output out_40,
  output out_41,
  output out_42,
  output out_43,
  output out_44,
  output out_45,
  output out_46,
  output out_47,
  output out_48,
  output out_49,
  output out_50
);

  wire \n4位全加器_2_out_10 , \n4位全加器_3_out_10 , \n4位全加器_4_out_10 ;

  \_4位全加器  \u_4位全加器_1  (
    .out_10(out_34), .out_11(out_35), .out_12(out_36), .out_13(out_37), .out_14(out_38), .in_1(in_2),
    .in_2(in_3), .in_3(in_10), .in_4(in_11), .in_5(in_18), .in_6(in_19), .in_7(in_26), .in_8(in_27),
    .in_9(\n4位全加器_2_out_10 ));
  \_4位全加器  \u_4位全加器_2  (
    .out_10(\n4位全加器_2_out_10 ), .out_11(out_39), .out_12(out_40), .out_13(out_41), .out_14(out_42),
    .in_1(in_4), .in_2(in_5), .in_3(in_12), .in_4(in_13), .in_5(in_20), .in_6(in_21), .in_7(in_28),
    .in_8(in_29), .in_9(\n4位全加器_3_out_10 ));
  \_4位全加器  \u_4位全加器_3  (
    .out_10(\n4位全加器_3_out_10 ), .out_11(out_43), .out_12(out_44), .out_13(out_45), .out_14(out_46),
    .in_1(in_6), .in_2(in_7), .in_3(in_14), .in_4(in_15), .in_5(in_22), .in_6(in_23), .in_7(in_30),
    .in_8(in_31), .in_9(\n4位全加器_4_out_10 ));
  \_4位全加器  \u_4位全加器_4  (
    .out_10(\n4位全加器_4_out_10 ), .out_11(out_47), .out_12(out_48), .out_13(out_49), .out_14(out_50),
    .in_1(in_8), .in_2(in_9), .in_3(in_16), .in_4(in_17), .in_5(in_24), .in_6(in_25), .in_7(in_32),
    .in_8(in_33), .in_9(in_1));
endmodule

module \_32位全加器  (
  input  in_1,
  input  [31:0] in_2,
  input  [31:0] in_3,
  output [31:0] out_4,
  output \向上进位 
);

  wire \n16位全加器_2_out_34 ;

  \_16位全加器  \u_16位全加器_1  (
    .out_34(\向上进位 ), .out_35(out_4[31]), .out_36(out_4[30]), .out_37(out_4[29]), .out_38(out_4[28]),
    .out_39(out_4[27]), .out_40(out_4[26]), .out_41(out_4[25]), .out_42(out_4[24]), .out_43(out_4[23]),
    .out_44(out_4[22]), .out_45(out_4[21]), .out_46(out_4[20]), .out_47(out_4[19]), .out_48(out_4[18]),
    .out_49(out_4[17]), .out_50(out_4[16]), .in_2(in_3[31]), .in_3(in_2[31]), .in_10(in_3[30]),
    .in_11(in_2[30]), .in_18(in_3[29]), .in_19(in_2[29]), .in_26(in_3[28]), .in_27(in_2[28]),
    .in_4(in_3[27]), .in_5(in_2[27]), .in_12(in_3[26]), .in_13(in_2[26]), .in_20(in_3[25]), .in_21(in_2[25]),
    .in_28(in_3[24]), .in_29(in_2[24]), .in_6(in_3[23]), .in_7(in_2[23]), .in_14(in_3[22]), .in_15(in_2[22]),
    .in_22(in_3[21]), .in_23(in_2[21]), .in_30(in_3[20]), .in_31(in_2[20]), .in_8(in_3[19]), .in_9(in_2[19]),
    .in_16(in_3[18]), .in_17(in_2[18]), .in_24(in_3[17]), .in_25(in_2[17]), .in_32(in_3[16]),
    .in_33(in_2[16]), .in_1(\n16位全加器_2_out_34 ));
  \_16位全加器  \u_16位全加器_2  (
    .out_34(\n16位全加器_2_out_34 ), .out_35(out_4[15]), .out_36(out_4[14]), .out_37(out_4[13]),
    .out_38(out_4[12]), .out_39(out_4[11]), .out_40(out_4[10]), .out_41(out_4[9]), .out_42(out_4[8]),
    .out_43(out_4[7]), .out_44(out_4[6]), .out_45(out_4[5]), .out_46(out_4[4]), .out_47(out_4[3]),
    .out_48(out_4[2]), .out_49(out_4[1]), .out_50(out_4[0]), .in_2(in_3[15]), .in_3(in_2[15]),
    .in_10(in_3[14]), .in_11(in_2[14]), .in_18(in_3[13]), .in_19(in_2[13]), .in_26(in_3[12]),
    .in_27(in_2[12]), .in_4(in_3[11]), .in_5(in_2[11]), .in_12(in_3[10]), .in_13(in_2[10]), .in_20(in_3[9]),
    .in_21(in_2[9]), .in_28(in_3[8]), .in_29(in_2[8]), .in_6(in_3[7]), .in_7(in_2[7]), .in_14(in_3[6]),
    .in_15(in_2[6]), .in_22(in_3[5]), .in_23(in_2[5]), .in_30(in_3[4]), .in_31(in_2[4]), .in_8(in_3[3]),
    .in_9(in_2[3]), .in_16(in_3[2]), .in_17(in_2[2]), .in_24(in_3[1]), .in_25(in_2[1]), .in_32(in_3[0]),
    .in_33(in_2[0]), .in_1(in_1));

  // Notes on the sheet:
  //   B[32:0]
  //   A[32:0]
endmodule

module \_32位全减器  (
  input  in_1,
  input  [31:0] in_2,
  input  [31:0] in_3,
  output [31:0] out_4
);

  wire [31:0] negator_1_out;

  \_32位全加器  \u_32位全加器_1  (.in_1(in_1), .in_3(in_2), .in_2(negator_1_out), .out_4(out_4));  // open: 向上进位
  Negator #(.width(32)) negator_1 (.in(in_3), .out(negator_1_out));

  // Notes on the sheet:
  //   A
  //   B
  //   SUB
endmodule

module ALU (
  input  [31:0] in_1,
  input  [31:0] in_2,
  input  [1:0] \选择端 ,
  output out_4,
  output [31:0] out_5,
  output out_6
);

  wire [31:0] and_1_out, \n32位全减器_1_out_4 , \n32位全加器_1_out_4 , or_1_out;

  assign or_1_out = in_1 | in_2;  // OR_Gate or_1, 32 bits wide
  assign and_1_out = in_1 & in_2;  // AND_Gate and_1, 32 bits wide
  \_32位全加器  \u_32位全加器_1  (.in_1(1'b0), .\向上进位 (out_4), .in_3(in_1), .in_2(in_2), .out_4(\n32位全加器_1_out_4 ));
  \_32位全减器  \u_32位全减器_1  (.in_2(in_1), .in_3(in_2), .out_4(\n32位全减器_1_out_4 ), .in_1(1'b0));
  Multiplexer #(.select(2), .width(32)) multiplexer_1 (
    .in0(\n32位全加器_1_out_4 ), .in1(\n32位全减器_1_out_4 ), .in2(and_1_out), .in3(or_1_out), .out(out_5),
    .sel(\选择端 ), .en(1'b1));
  Comparator #(.width(32)) comparator_1 (.a(out_5), .b({32{1'b0}}), .eq(out_6));  // open: gt, lt
endmodule

module \立即数扩展电路  (
  input  [15:0] in_1,
  input  [1:0] Extsel,
  output [31:0] out_3
);

  wire [31:0] bit_extender_1_out, bit_extender_2_out;

  assign bit_extender_1_out = {{16{1'b0}}, in_1};  // Bit_Extender bit_extender_1
  assign bit_extender_2_out = {{16{in_1[15]}}, in_1};  // Bit_Extender bit_extender_2
  Multiplexer #(.select(2), .width(32)) multiplexer_1 (
    .in0(bit_extender_1_out), .in1(bit_extender_2_out), .in2({in_1, {16{1'b0}}}), .out(out_3), .sel(Extsel),
    .en(1'b1));  // open: in3

  // Notes on the sheet:
  //   Imm16
  //   ExtImm32
endmodule

module \_7条MIPS指令的译码电路  (
  input  [5:0] opcode,
  input  [5:0] funct,
  output addu,
  output subu,
  output ori,
  output lui,
  output lw,
  output sw,
  output beq
);

  wire not_1_out, not_2_out, not_3_out, not_4_out, not_5_out, not_6_out, not_7_out, not_8_out, not_9_out,
       not_10_out, not_11_out, not_12_out, not_13_out, not_14_out, not_15_out, not_16_out, not_17_out,
       not_18_out, not_19_out, not_20_out, not_21_out, not_22_out, not_23_out, not_24_out, not_25_out,
       not_26_out, not_27_out, not_28_out, not_29_out, not_30_out, not_31_out, not_32_out, not_33_out,
       not_34_out;

  and and_1 (addu, not_2_out, not_1_out, not_3_out, not_5_out, not_4_out, not_6_out, funct[0], not_9_out, not_7_out, not_10_out, not_8_out, funct[5]);
  not not_1 (not_1_out, opcode[1]);
  not not_2 (not_2_out, opcode[0]);
  not not_3 (not_3_out, opcode[2]);
  not not_4 (not_4_out, opcode[4]);
  not not_5 (not_5_out, opcode[3]);
  not not_6 (not_6_out, opcode[5]);
  not not_7 (not_7_out, funct[2]);
  not not_8 (not_8_out, funct[4]);
  not not_9 (not_9_out, funct[1]);
  not not_10 (not_10_out, funct[3]);
  and and_2 (subu, not_11_out, not_12_out, not_14_out, not_13_out, not_15_out, not_16_out, funct[0], funct[1], not_18_out, not_17_out, not_19_out, funct[5]);
  not not_11 (not_11_out, opcode[0]);
  not not_12 (not_12_out, opcode[1]);
  not not_13 (not_13_out, opcode[3]);
  not not_14 (not_14_out, opcode[2]);
  not not_15 (not_15_out, opcode[4]);
  not not_16 (not_16_out, opcode[5]);
  not not_17 (not_17_out, funct[3]);
  not not_18 (not_18_out, funct[2]);
  not not_19 (not_19_out, funct[4]);
  not not_20 (not_20_out, opcode[1]);
  and and_3 (ori, opcode[0], not_20_out, opcode[2], opcode[3], not_21_out, not_22_out);
  not not_21 (not_21_out, opcode[4]);
  not not_22 (not_22_out, opcode[5]);
  and and_4 (lui, opcode[0], opcode[1], opcode[2], opcode[3], not_23_out, not_24_out);
  not not_23 (not_23_out, opcode[4]);
  not not_24 (not_24_out, opcode[5]);
  and and_5 (lw, opcode[0], opcode[1], not_25_out, not_26_out, not_27_out, opcode[5]);
  not not_25 (not_25_out, opcode[2]);
  not not_26 (not_26_out, opcode[3]);
  not not_27 (not_27_out, opcode[4]);
  and and_6 (sw, opcode[0], opcode[1], not_28_out, opcode[3], not_29_out, opcode[5]);
  not not_28 (not_28_out, opcode[2]);
  not not_29 (not_29_out, opcode[4]);
  and and_7 (beq, not_33_out, not_30_out, opcode[2], not_31_out, not_32_out, not_34_out);
  not not_30 (not_30_out, opcode[1]);
  not not_31 (not_31_out, opcode[3]);
  not not_32 (not_32_out, opcode[4]);
  not not_33 (not_33_out, opcode[0]);
  not not_34 (not_34_out, opcode[5]);

  // Notes on the sheet:
  //   Mdec_20020203
endmodule

module \编码器  (
  input  [6:0] in_1,
  input  zero,
  output [1:0] ALU_sel,
  output [1:0] EXT_sel,
  output B_sel,
  output PC_sel
);

  wire and_2_out, and_3_out, and_5_out, and_6_out, not_1_out, not_2_out, not_3_out, not_4_out, not_5_out,
       not_6_out, not_7_out, not_8_out, not_9_out, not_10_out, not_11_out, not_12_out, not_13_out,
       not_14_out, not_15_out, not_16_out, not_17_out, not_18_out, not_19_out, not_20_out, not_21_out,
       not_22_out, not_23_out, not_24_out, not_25_out, not_26_out, not_27_out, not_28_out, not_29_out,
       not_30_out, not_31_out, not_32_out, not_33_out, not_34_out, not_35_out, not_36_out;

  not not_1 (not_1_out, in_1[0]);
  not not_2 (not_2_out, in_1[1]);
  not not_3 (not_3_out, in_1[2]);
  not not_4 (not_4_out, in_1[3]);
  not not_5 (not_5_out, in_1[5]);
  not not_6 (not_6_out, in_1[6]);
  not not_7 (not_7_out, in_1[0]);
  not not_8 (not_8_out, in_1[1]);
  not not_9 (not_9_out, in_1[2]);
  not not_10 (not_10_out, in_1[3]);
  not not_11 (not_11_out, in_1[4]);
  not not_12 (not_12_out, in_1[6]);
  not not_13 (not_13_out, in_1[1]);
  not not_14 (not_14_out, in_1[2]);
  not not_15 (not_15_out, in_1[3]);
  not not_16 (not_16_out, in_1[4]);
  not not_17 (not_17_out, in_1[5]);
  not not_18 (not_18_out, in_1[6]);
  not not_19 (not_19_out, in_1[0]);
  not not_20 (not_20_out, in_1[1]);
  not not_21 (not_21_out, in_1[2]);
  not not_22 (not_22_out, in_1[4]);
  not not_23 (not_23_out, in_1[5]);
  not not_24 (not_24_out, in_1[6]);
  not not_25 (not_25_out, in_1[0]);
  not not_26 (not_26_out, in_1[1]);
  not not_27 (not_27_out, in_1[3]);
  not not_28 (not_28_out, in_1[4]);
  not not_29 (not_29_out, in_1[5]);
  not not_30 (not_30_out, in_1[6]);
  not not_31 (not_31_out, in_1[0]);
  not not_32 (not_32_out, in_1[2]);
  not not_33 (not_33_out, in_1[3]);
  not not_34 (not_34_out, in_1[4]);
  not not_35 (not_35_out, in_1[5]);
  not not_36 (not_36_out, in_1[6]);
  and and_1 (ALU_sel[1], not_1_out, not_2_out, not_3_out, not_4_out, in_1[4], not_5_out, not_6_out);
  and and_2 (and_2_out, not_7_out, not_8_out, not_9_out, not_10_out, not_11_out, in_1[5], not_12_out);
  and and_3 (and_3_out, in_1[0], not_13_out, not_14_out, not_15_out, not_16_out, not_17_out, not_18_out);
  and and_4 (EXT_sel[1], not_19_out, not_20_out, not_21_out, in_1[3], not_22_out, not_23_out, not_24_out);
  and and_5 (and_5_out, not_25_out, not_26_out, in_1[2], not_27_out, not_28_out, not_29_out, not_30_out);
  and and_6 (and_6_out, not_31_out, in_1[1], not_32_out, not_33_out, not_34_out, not_35_out, not_36_out);
  or or_1 (ALU_sel[0], ALU_sel[1], and_2_out, and_3_out);
  or or_2 (EXT_sel[0], and_5_out, and_6_out);
  or or_3 (B_sel, ALU_sel[1], EXT_sel[1], and_5_out, and_6_out);
  and and_7 (PC_sel, and_3_out, zero);
endmodule

module \综合验证  (
  input  [5:0] in_1,
  input  [5:0] in_2,
  input  [31:0] in_3,
  input  [31:0] in_4,
  input  [15:0] in_5,
  output PC_sel,
  output [31:0] out_7
);

  wire alu_1_out_6, \编码器_1_b_sel ;
  wire [1:0] \编码器_1_alu_sel , \编码器_1_ext_sel ;
  wire [6:0] \n7条mips指令的译码电路_1_beq ;
  wire [31:0] multiplexer_1_out, \立即数扩展电路_1_out_3 ;

  \立即数扩展电路  \u_立即数扩展电路_1  (.in_1(in_5), .out_3(\立即数扩展电路_1_out_3 ), .Extsel(\编码器_1_ext_sel ));
  \_7条MIPS指令的译码电路  \u_7条mips指令的译码电路_1  (
    .addu(\n7条mips指令的译码电路_1_beq [6]), .subu(\n7条mips指令的译码电路_1_beq [5]), .ori(\n7条mips指令的译码电路_1_beq [4]),
    .lui(\n7条mips指令的译码电路_1_beq [3]), .lw(\n7条mips指令的译码电路_1_beq [2]), .sw(\n7条mips指令的译码电路_1_beq [1]),
    .beq(\n7条mips指令的译码电路_1_beq [0]), .opcode(in_1), .funct(in_2));
  Multiplexer #(.width(32)) multiplexer_1 (
    .in0(in_4), .in1(\立即数扩展电路_1_out_3 ), .out(multiplexer_1_out), .sel(\编码器_1_b_sel ), .en(1'b1));
  ALU alu_1 (
    .in_1(in_3), .in_2(multiplexer_1_out), .out_5(out_7), .\选择端 (\编码器_1_alu_sel ), .out_6(alu_1_out_6));  // open: out_4
  \编码器  \u_编码器_1  (
    .in_1(\n7条mips指令的译码电路_1_beq ), .zero(alu_1_out_6), .ALU_sel(\编码器_1_alu_sel ), .EXT_sel(\编码器_1_ext_sel ),
    .B_sel(\编码器_1_b_sel ), .PC_sel(PC_sel));

  // Notes on the sheet:
  //   A
  //   B
endmodule
