// Logisim project 单周期处理器开发-王思哲20020203.circ as structural Verilog: 10 circuits, main circuit main
module main (
  input  in_1
);

  wire ALUSrc, clk, J, MemToReg, MemWrite, nPC_sel, RegDst, RegWrite, zero;
  wire [1:0] ALUOp, ExtOp;
  wire [4:0] multiplexer_1_out, rs, rt;
  wire [5:0] funct, opcode;
  wire [15:6] imm16;
  wire [31:0] alu_1_out_5, DataToGPR, \dm_1_数据输出 , \ext_1_立即数扩展输出ext32 , gpr_1_out_8, gpr_1_out_9,
       multiplexer_2_out;

  Clock #(.highDuration(1), .lowDuration(1)) clock_1 (.out(clk));
  Multiplexer #(.select(1), .width(5), .disabled("Z"), .enable("false")) multiplexer_1 (
    .in0(rt), .in1(imm16[15:11]), .out(multiplexer_1_out), .sel(RegDst));
  // Probe on {opcode, rs, rt, imm16, funct}
  IFUwithJ ifuwithj_1 (
    .nPC_sel(nPC_sel), .zero(zero), .clk(clk), .reset(in_1), .ins({opcode, rs, rt, imm16, funct}), .J(J));
  // Probe on opcode
  GPR gpr_1 (
    .in_2(clk), .in_3(RegWrite), .in_4(DataToGPR), .in_5(rs), .in_6(rt), .in_7(multiplexer_1_out),
    .out_8(gpr_1_out_8), .out_9(gpr_1_out_9), .in_1(in_1));
  // Probe on RegWrite
  EXT ext_1 (.\立即数扩展输入imm16 ({imm16, funct}), .\立即数扩展输出ext32 (\ext_1_立即数扩展输出ext32 ), .ExtOp(ExtOp));
  // Probe on ExtOp
  // Probe on \ext_1_立即数扩展输出ext32 
  // Probe on funct
  // Probe on {imm16, funct}
  Multiplexer #(.select(1), .width(32), .disabled("Z"), .enable("false")) multiplexer_2 (
    .in0(gpr_1_out_8), .in1(\ext_1_立即数扩展输出ext32 ), .out(multiplexer_2_out), .sel(ALUSrc));
  // Probe on ALUSrc
  // Probe on opcode
  // Probe on ALUOp
  ALU alu_1 (.A(gpr_1_out_9), .B(multiplexer_2_out), .out_5(alu_1_out_5), .in_3(ALUOp), .zero(zero));
  Multiplexer #(.select(1), .width(32), .disabled("Z"), .enable("false")) multiplexer_3 (
    .in0(alu_1_out_5), .in1(\dm_1_数据输出 ), .out(DataToGPR), .sel(MemToReg));
  DM dm_1 (.in_1(clk), .in_2(in_1), .in_3(MemWrite), .\地址 (alu_1_out_5), .\数据 (gpr_1_out_8), .\数据输出 (\dm_1_数据输出 ));
  // Probe on funct
  Controller controller_1 (
    .opcode(opcode), .funct(funct), .RegDst(RegDst), .RegWrite(RegWrite), .ALUSrc(ALUSrc),
    .MemtoReg(MemToReg), .MemWrite(MemWrite), .Branch(nPC_sel), .ALUOp_1_0(ALUOp), .EXTOp_1_0(ExtOp), .J(J));
  // Probe on MemToReg

  // Other names for the same wires on the sheet: imm16[5:0] = funct; rd[4:0] = imm16[15:11]; reset = in_1

  // Notes on the sheet:
  //   TUNNEL LIST
endmodule

module EXT (
  input  [15:0] \立即数扩展输入imm16 ,
  input  [1:0] ExtOp,
  output [31:0] \立即数扩展输出ext32 
);

  wire [31:0] bit_extender_1_out, bit_extender_2_out;

  assign bit_extender_1_out = {{16{1'b0}}, \立即数扩展输入imm16 };  // Bit_Extender bit_extender_1
  assign bit_extender_2_out = {{16{\立即数扩展输入imm16 [15]}}, \立即数扩展输入imm16 };  // Bit_Extender bit_extender_2
  Multiplexer #(.select(2), .width(32), .disabled("Z"), .enable("false")) multiplexer_1 (
    .in0(bit_extender_1_out), .in1(bit_extender_2_out), .in2({\立即数扩展输入imm16 , {16{1'b0}}}),
    .out(\立即数扩展输出ext32 ), .sel(ExtOp));  // open: in3

  // Notes on the sheet:
  //   立即数置到高位，低位0扩展
  //   高位0扩展，低位立即数
  //   高位符号扩展，低位立即数
endmodule

module Controller (
  input  [5:0] opcode,
  input  [5:0] funct,
  output RegDst,
  output RegWrite,
  output ALUSrc,
  output MemtoReg,
  output MemWrite,
  output Branch,
  output [1:0] ALUOp_1_0,
  output [1:0] EXTOp_1_0,
  output J
);

  wire addu_out, beq_out, j_out, lw_out, not_1_out, not_2_out, not_3_out, not_4_out, not_5_out, not_6_out,
       not_7_out, not_8_out, not_9_out, not_10_out, not_11_out, not_12_out, ori_out, subu_out, sw_out;

  not not_1 (not_1_out, opcode[5]);
  not not_2 (not_2_out, opcode[4]);
  not not_3 (not_3_out, opcode[3]);
  not not_4 (not_4_out, opcode[2]);
  not not_5 (not_5_out, opcode[1]);
  not not_6 (not_6_out, opcode[0]);
  not not_7 (not_7_out, funct[5]);
  not not_8 (not_8_out, funct[4]);
  and ori (ori_out, not_1_out, not_2_out, opcode[3], opcode[2], not_5_out, opcode[0]);
  and lw (lw_out, opcode[5], not_2_out, not_3_out, not_4_out, opcode[1], opcode[0]);
  and sw (sw_out, opcode[5], not_2_out, opcode[3], not_4_out, opcode[1], opcode[0]);
  and beq (beq_out, not_1_out, not_2_out, not_3_out, opcode[2], not_5_out, not_6_out);
  and lui (EXTOp_1_0[1], not_1_out, not_2_out, opcode[3], opcode[2], opcode[1], opcode[0]);
  and u_j (j_out, not_1_out, not_2_out, not_3_out, not_4_out, opcode[1], not_6_out);
  not not_9 (not_9_out, funct[3]);
  not not_10 (not_10_out, funct[2]);
  not not_11 (not_11_out, funct[1]);
  not not_12 (not_12_out, funct[0]);
  and addu (addu_out, not_1_out, not_2_out, not_3_out, not_4_out, not_5_out, not_6_out, funct[5], not_8_out, not_9_out, not_10_out, not_11_out, funct[0]);
  and subu (subu_out, not_1_out, not_2_out, not_3_out, not_4_out, not_5_out, not_6_out, funct[5], not_8_out, not_9_out, not_10_out, funct[1], funct[0]);
  or u_RegDst (RegDst, addu_out, subu_out);
  or u_RegWrite (RegWrite, addu_out, subu_out, ori_out, lw_out, EXTOp_1_0[1]);
  or u_ALUSrc (ALUSrc, ori_out, lw_out, EXTOp_1_0[1], sw_out);
  buf u_MemtoReg (MemtoReg, lw_out);  // OR_Gate
  buf u_MemWrite (MemWrite, sw_out);  // OR_Gate
  buf u_Branch (Branch, beq_out);  // OR_Gate
  buf ALUOp1 (ALUOp_1_0[1], ori_out);  // OR_Gate
  or ALUOp0 (ALUOp_1_0[0], subu_out, beq_out);
  or ExtOp0 (EXTOp_1_0[0], lw_out, sw_out);
  buf J_2 (J, j_out);  // OR_Gate
endmodule

module ALU (
  input  [31:0] A,
  input  [31:0] B,
  input  [1:0] in_3,
  output zero,
  output [31:0] out_5
);

  wire [31:0] \n32位组间并组内并加法器_1_out_5 , or_1_out, subtractor_1_out;

  // Probe on B
  // Probe on A
  \_32位组间并组内并加法器  \u_32位组间并组内并加法器_1  (
    .A32___A1(A), .B32___B1(B), .out_5(\n32位组间并组内并加法器_1_out_5 ), .C0(1'b0));  // open: 进位
  Subtractor #(.width(32)) subtractor_1 (.a(A), .b(B), .out(subtractor_1_out));  // open: bin, bout
  assign or_1_out = A | B;  // OR_Gate or_1, 32 bits wide
  Comparator #(.width(32), .mode("unsigned")) comparator_1 (.a({32{1'b0}}), .b(out_5), .eq(zero));  // open: gt, lt
  Multiplexer #(.select(2), .width(32), .disabled("Z"), .enable("false")) multiplexer_1 (
    .in0(\n32位组间并组内并加法器_1_out_5 ), .in1(subtractor_1_out), .in2(or_1_out), .out(out_5), .sel(in_3));  // open: in3
  // Probe on out_5
endmodule

module \_4位并行加法器  (
  input  C0,
  input  [3:0] A4A3A2A1,
  input  [3:0] B4B3B2B1,
  output G1_star,
  output P1_star,
  output C3,
  output C2,
  output C1,
  output [3:0] tmp
);

  wire and_1_out, and_4_out, and_7_out, and_9_out, and_10_out, and_11_out, and_12_out, and_13_out,
       and_14_out, G1, G2, G3, G4, P1, P2, P3, P4;

  and and_1 (and_1_out, P4, G3);
  and and_2 (G3, A4A3A2A1[2], B4B3B2B1[2]);
  and and_3 (G4, A4A3A2A1[3], B4B3B2B1[3]);
  or or_1 (G1_star, G4, and_1_out, and_4_out, and_7_out);
  and and_4 (and_4_out, P4, P3, G2);
  and and_5 (G2, A4A3A2A1[1], B4B3B2B1[1]);
  and and_6 (G1, A4A3A2A1[0], B4B3B2B1[0]);
  and and_7 (and_7_out, P4, P3, P2, G1);
  and and_8 (P1_star, P4, P3, P2, P1);
  xor xor_1 (P4, A4A3A2A1[3], B4B3B2B1[3]);
  and and_9 (and_9_out, P3, G2);
  xor xor_2 (P3, A4A3A2A1[2], B4B3B2B1[2]);
  xor xor_3 (tmp[3], P4, C3);
  xor xor_4 (tmp[2], P3, C2);
  or or_2 (C3, G3, and_9_out, and_11_out, and_10_out);
  and and_10 (and_10_out, P3, P2, P1, C0);
  and and_11 (and_11_out, P3, P2, G1);
  xor xor_5 (P1, A4A3A2A1[0], B4B3B2B1[0]);
  xor xor_6 (P2, A4A3A2A1[1], B4B3B2B1[1]);
  xor xor_7 (tmp[1], P2, C1);
  xor xor_8 (tmp[0], P1, C0);
  or or_3 (C2, G2, and_13_out, and_12_out);
  and and_12 (and_12_out, P2, P1, C0);
  and and_13 (and_13_out, P2, G1);
  or or_4 (C1, G1, and_14_out);
  and and_14 (and_14_out, P1, C0);

  // Other names for the same wires on the sheet: A1 = A4A3A2A1[0]; A2 = A4A3A2A1[1]; A3 = A4A3A2A1[2];
  //   A4 = A4A3A2A1[3]; B1 = B4B3B2B1[0]; B2 = B4B3B2B1[1]; B3 = B4B3B2B1[2]; B4 = B4B3B2B1[3]; t1 = tmp[0];
  //   t2 = tmp[1]; t3 = tmp[2]; t4 = tmp[3]

  // Notes on the sheet:
  //   IN
  //   OUT
endmodule

module \_8位并行加法器  (
  input  in_1,
  input  [7:0] A8___A1,
  input  [7:0] B8___B1,
  output G_star,
  output P_star,
  output [7:0] OUT
);

  wire and_1_out, and_2_out, \n4位并行加法器_1_g1_star , \n4位并行加法器_1_p1_star , \n4位并行加法器_2_g1_star ,
       \n4位并行加法器_2_p1_star , tunnel;

  or or_1 (G_star, \n4位并行加法器_1_g1_star , and_1_out);
  and and_1 (and_1_out, \n4位并行加法器_1_p1_star , \n4位并行加法器_2_g1_star );
  \_4位并行加法器  \u_4位并行加法器_1  (
    .C0(tunnel), .G1_star(\n4位并行加法器_1_g1_star ), .P1_star(\n4位并行加法器_1_p1_star ), .A4A3A2A1(A8___A1[7:4]),
    .tmp(OUT[7:4]), .B4B3B2B1(B8___B1[7:4]));  // open: C3, C2, C1
  or or_2 (tunnel, \n4位并行加法器_2_g1_star , and_2_out);
  and and_2 (and_2_out, \n4位并行加法器_2_p1_star , in_1);
  and and_3 (P_star, \n4位并行加法器_1_p1_star , \n4位并行加法器_2_p1_star );
  \_4位并行加法器  \u_4位并行加法器_2  (
    .C0(in_1), .G1_star(\n4位并行加法器_2_g1_star ), .P1_star(\n4位并行加法器_2_p1_star ), .A4A3A2A1(A8___A1[3:0]),
    .tmp(OUT[3:0]), .B4B3B2B1(B8___B1[3:0]));  // open: C3, C2, C1

  // Other names for the same wires on the sheet: OUT4___OUT1[3:0] = OUT[3:0]; OUT8___OUT5[3:0] = OUT[7:4]
endmodule

module \_32位组间并组内并加法器  (
  input  C0,
  input  [31:0] A32___A1,
  input  [31:0] B32___B1,
  output \进位 ,
  output [31:0] out_5
);

  wire and_1_out, and_2_out, and_3_out, and_4_out, and_5_out, and_6_out, and_7_out, and_8_out, and_9_out,
       and_10_out, C8, C16, C24, G1, G2, G3, G4, P1, P2, P3, P4;

  and and_1 (and_1_out, P4, G3);
  or or_1 (\进位 , G4, and_1_out, and_2_out, and_3_out, and_4_out);
  and and_2 (and_2_out, P4, P3, G2);
  \_8位并行加法器  \u_8位并行加法器_1  (
    .in_1(C24), .G_star(G4), .P_star(P4), .OUT(out_5[31:24]), .A8___A1(A32___A1[31:24]),
    .B8___B1(B32___B1[31:24]));
  and and_3 (and_3_out, P4, P3, P2, G1);
  and and_4 (and_4_out, P4, P3, P2, P1, C0);
  \_8位并行加法器  \u_8位并行加法器_2  (
    .in_1(C16), .G_star(G3), .P_star(P3), .OUT(out_5[23:16]), .A8___A1(A32___A1[23:16]),
    .B8___B1(B32___B1[23:16]));
  or or_2 (C24, G3, and_6_out, and_5_out, and_7_out);
  and and_5 (and_5_out, P3, P2, G1);
  and and_6 (and_6_out, P3, G2);
  and and_7 (and_7_out, P3, P2, P1, C0);
  \_8位并行加法器  \u_8位并行加法器_3  (
    .in_1(C8), .G_star(G2), .P_star(P2), .OUT(out_5[15:8]), .A8___A1(A32___A1[15:8]), .B8___B1(B32___B1[15:8]));
  or or_3 (C16, G2, and_8_out, and_9_out);
  and and_8 (and_8_out, P2, G1);
  and and_9 (and_9_out, P2, P1, C0);
  \_8位并行加法器  \u_8位并行加法器_4  (
    .in_1(C0), .G_star(G1), .P_star(P1), .OUT(out_5[7:0]), .A8___A1(A32___A1[7:0]), .B8___B1(B32___B1[7:0]));
  or or_4 (C8, G1, and_10_out);
  and and_10 (and_10_out, P1, C0);

  // Other names for the same wires on the sheet: OUT8___0UT1[7:0] = out_5[7:0]; OUT16___0UT9[7:0] = out_5[15:8];
  //   OUT24___0UT17[7:0] = out_5[23:16]; OUT32___0UT25[7:0] = out_5[31:24]
endmodule

module GPR (
  input  in_1,
  input  in_2,
  input  in_3,
  input  [31:0] in_4,
  input  [4:0] in_5,
  input  [4:0] in_6,
  input  [4:0] in_7,
  output [31:0] out_8,
  output [31:0] out_9
);

  wire _0_IN, _1_IN, _2_IN, _3_IN, _4_IN, _5_IN, _6_IN, _7_IN, _8_IN, _9_IN, _10_IN, _11_IN, _12_IN, _13_IN,
       _14_IN, _15_IN, _16_IN, _17_IN, _18_IN, _19_IN, _20_IN, _21_IN, _22_IN, _23_IN, _24_IN, _25_IN,
       _26_IN, _27_IN, _28_IN, _29_IN, _30_IN, _31_IN;
  wire [31:0] _0_OUT, _1_OUT, _2_OUT, _3_OUT, _4_OUT, _5_OUT, _6_OUT, _7_OUT, _8_OUT, _9_OUT, _10_OUT,
       _11_OUT, _12_OUT, _13_OUT, _14_OUT, _15_OUT, _16_OUT, _17_OUT, _18_OUT, _19_OUT, _20_OUT, _21_OUT,
       _22_OUT, _23_OUT, _24_OUT, _25_OUT, _26_OUT, _27_OUT, _28_OUT, _29_OUT, _30_OUT, _31_OUT;

  Register #(.width(32), .trigger("rising"), .Select("low")) register_1 (
    .D({32{1'b0}}), .en(_0_IN), .Q(_0_OUT), .clk(in_2), .clr(in_1));
  Register #(.width(32), .trigger("rising"), .Select("low")) register_2 (
    .D(in_4), .en(_1_IN), .Q(_1_OUT), .clk(in_2), .clr(in_1));
  Register #(.width(32), .trigger("rising"), .Select("low")) register_3 (
    .D(in_4), .en(_2_IN), .Q(_2_OUT), .clk(in_2), .clr(in_1));
  Register #(.width(32), .trigger("rising"), .Select("low")) register_4 (
    .D(in_4), .en(_3_IN), .Q(_3_OUT), .clk(in_2), .clr(in_1));
  Register #(.width(32), .trigger("rising"), .Select("low")) register_5 (
    .D(in_4), .en(_4_IN), .Q(_4_OUT), .clk(in_2), .clr(in_1));
  Register #(.width(32), .trigger("rising"), .Select("low")) register_6 (
    .D(in_4), .en(_5_IN), .Q(_5_OUT), .clk(in_2), .clr(in_1));
  Register #(.width(32), .trigger("rising"), .Select("low")) register_7 (
    .D(in_4), .en(_6_IN), .Q(_6_OUT), .clk(in_2), .clr(in_1));
  Register #(.width(32), .trigger("rising"), .Select("low")) register_8 (
    .D(in_4), .en(_7_IN), .Q(_7_OUT), .clk(in_2), .clr(in_1));
  Demultiplexer #(.select(5), .width(1), .tristate("false"), .disabled("Z"), .enable("false")) demultiplexer_1 (
    .out0(_0_IN), .out1(_1_IN), .out2(_2_IN), .out3(_3_IN), .out4(_4_IN), .out5(_5_IN), .out6(_6_IN),
    .out7(_7_IN), .out8(_8_IN), .out9(_9_IN), .out10(_10_IN), .out11(_11_IN), .out12(_12_IN), .out13(_13_IN),
    .out14(_14_IN), .out15(_15_IN), .out16(_16_IN), .out17(_17_IN), .out18(_18_IN), .out19(_19_IN),
    .out20(_20_IN), .out21(_21_IN), .out22(_22_IN), .out23(_23_IN), .out24(_24_IN), .out25(_25_IN),
    .out26(_26_IN), .out27(_27_IN), .out28(_28_IN), .out29(_29_IN), .out30(_30_IN), .out31(_31_IN),
    .in(in_3), .sel(in_7));
  Register #(.width(32), .trigger("rising"), .Select("low")) register_9 (
    .D(in_4), .en(_8_IN), .Q(_8_OUT), .clk(in_2), .clr(in_1));
  Register #(.width(32), .trigger("rising"), .Select("low")) register_10 (
    .D(in_4), .en(_9_IN), .Q(_9_OUT), .clk(in_2), .clr(in_1));
  Register #(.width(32), .trigger("rising"), .Select("low")) register_11 (
    .D(in_4), .en(_10_IN), .Q(_10_OUT), .clk(in_2), .clr(in_1));
  Register #(.width(32), .trigger("rising"), .Select("low")) register_12 (
    .D(in_4), .en(_11_IN), .Q(_11_OUT), .clk(in_2), .clr(in_1));
  Register #(.width(32), .trigger("rising"), .Select("low")) register_13 (
    .D(in_4), .en(_12_IN), .Q(_12_OUT), .clk(in_2), .clr(in_1));
  Register #(.width(32), .trigger("rising"), .Select("low")) register_14 (
    .D(in_4), .en(_13_IN), .Q(_13_OUT), .clk(in_2), .clr(in_1));
  Register #(.width(32), .trigger("rising"), .Select("low")) register_15 (
    .D(in_4), .en(_14_IN), .Q(_14_OUT), .clk(in_2), .clr(in_1));
  Register #(.width(32), .trigger("rising"), .Select("low")) register_16 (
    .D(in_4), .en(_15_IN), .Q(_15_OUT), .clk(in_2), .clr(in_1));
  Multiplexer #(.select(5), .width(32), .disabled("Z"), .enable("false")) multiplexer_1 (
    .in0(_0_OUT), .in1(_1_OUT), .in2(_2_OUT), .in3(_3_OUT), .in4(_4_OUT), .in5(_5_OUT), .in6(_6_OUT),
    .in7(_7_OUT), .in8(_8_OUT), .in9(_9_OUT), .in10(_10_OUT), .in11(_11_OUT), .in12(_12_OUT), .in13(_13_OUT),
    .in14(_14_OUT), .in15(_15_OUT), .in16(_16_OUT), .in17(_17_OUT), .in18(_18_OUT), .in19(_19_OUT),
    .in20(_20_OUT), .in21(_21_OUT), .in22(_22_OUT), .in23(_23_OUT), .in24(_24_OUT), .in25(_25_OUT),
    .in26(_26_OUT), .in27(_27_OUT), .in28(_28_OUT), .in29(_29_OUT), .in30(_30_OUT), .in31(_31_OUT),
    .out(out_8), .sel(in_6));
  Register #(.width(32), .trigger("rising"), .Select("low")) register_17 (
    .D(in_4), .en(_16_IN), .Q(_16_OUT), .clk(in_2), .clr(in_1));
  Register #(.width(32), .trigger("rising"), .Select("low")) register_18 (
    .D(in_4), .en(_17_IN), .Q(_17_OUT), .clk(in_2), .clr(in_1));
  Register #(.width(32), .trigger("rising"), .Select("low")) register_19 (
    .D(in_4), .en(_18_IN), .Q(_18_OUT), .clk(in_2), .clr(in_1));
  Register #(.width(32), .trigger("rising"), .Select("low")) register_20 (
    .D(in_4), .en(_19_IN), .Q(_19_OUT), .clk(in_2), .clr(in_1));
  Multiplexer #(.select(5), .width(32), .disabled("Z"), .enable("false")) multiplexer_2 (
    .in0(_0_OUT), .in1(_1_OUT), .in2(_2_OUT), .in3(_3_OUT), .in4(_4_OUT), .in5(_5_OUT), .in6(_6_OUT),
    .in7(_7_OUT), .in8(_8_OUT), .in9(_9_OUT), .in10(_10_OUT), .in11(_11_OUT), .in12(_12_OUT), .in13(_13_OUT),
    .in14(_14_OUT), .in15(_15_OUT), .in16(_16_OUT), .in17(_17_OUT), .in18(_18_OUT), .in19(_19_OUT),
    .in20(_20_OUT), .in21(_21_OUT), .in22(_22_OUT), .in23(_23_OUT), .in24(_24_OUT), .in25(_25_OUT),
    .in26(_26_OUT), .in27(_27_OUT), .in28(_28_OUT), .in29(_29_OUT), .in30(_30_OUT), .in31(_31_OUT),
    .out(out_9), .sel(in_5));
  Register #(.width(32), .trigger("rising"), .Select("low")) register_21 (
    .D(in_4), .en(_20_IN), .Q(_20_OUT), .clk(in_2), .clr(in_1));
  Register #(.width(32), .trigger("rising"), .Select("low")) register_22 (
    .D(in_4), .en(_21_IN), .Q(_21_OUT), .clk(in_2), .clr(in_1));
  Register #(.width(32), .trigger("rising"), .Select("low")) register_23 (
    .D(in_4), .en(_22_IN), .Q(_22_OUT), .clk(in_2), .clr(in_1));
  Register #(.width(32), .trigger("rising"), .Select("low")) register_24 (
    .D(in_4), .en(_23_IN), .Q(_23_OUT), .clk(in_2), .clr(in_1));
  Register #(.width(32), .trigger("rising"), .Select("low")) register_25 (
    .D(in_4), .en(_24_IN), .Q(_24_OUT), .clk(in_2), .clr(in_1));
  Register #(.width(32), .trigger("rising"), .Select("low")) register_26 (
    .D(in_4), .en(_25_IN), .Q(_25_OUT), .clk(in_2), .clr(in_1));
  Register #(.width(32), .trigger("rising"), .Select("low")) register_27 (
    .D(in_4), .en(_26_IN), .Q(_26_OUT), .clk(in_2), .clr(in_1));
  Register #(.width(32), .trigger("rising"), .Select("low")) register_28 (
    .D(in_4), .en(_27_IN), .Q(_27_OUT), .clk(in_2), .clr(in_1));
  Register #(.width(32), .trigger("rising"), .Select("low")) register_29 (
    .D(in_4), .en(_28_IN), .Q(_28_OUT), .clk(in_2), .clr(in_1));
  Register #(.width(32), .trigger("rising"), .Select("low")) register_30 (
    .D(in_4), .en(_29_IN), .Q(_29_OUT), .clk(in_2), .clr(in_1));
  Register #(.width(32), .trigger("rising"), .Select("low")) register_31 (
    .D(in_4), .en(_30_IN), .Q(_30_OUT), .clk(in_2), .clr(in_1));
  Register #(.width(32), .trigger("rising"), .Select("low")) register_32 (
    .D(in_4), .en(_31_IN), .Q(_31_OUT), .clk(in_2), .clr(in_1));

  // Other names for the same wires on the sheet: A1_OUT[31:0] = out_9; A1_RA[4:0] = in_5; A2_OUT[31:0] = out_8;
  //   A2_RA[4:0] = in_6; A3_WA[4:0] = in_7; CLK = in_2; RegWrite = in_3; reset = in_1; WD[31:0] = in_4
endmodule

module IFUwithJ (
  input  J,
  input  nPC_sel,
  input  zero,
  input  clk,
  input  reset,
  output [31:0] ins
);

  wire _28, _29, _30, _31, and_1_out;
  wire [7:0] pc_q_2;
  wire [9:0] pc_q_4;
  wire [10:0] pc_q, pc_q_3;
  wire [27:0] adder_1_out;
  wire [31:0] adder_2_out, bit_extender_1_out, multiplexer_1_out, multiplexer_2_out, shifter_1_out;

  assign bit_extender_1_out = {{16{ins[15]}}, ins[15:0]};  // Bit_Extender bit_extender_1
  Shifter #(.width(32), .shift("ll")) shifter_1 (.in(bit_extender_1_out), .\dist (5'b00010), .out(shifter_1_out));
  Adder #(.width(32)) adder_1 (
    .a({pc_q_4, pc_q_3, pc_q[10], pc_q_2, pc_q[1:0]}), .b(32'h4), .out({_31, _30, _29, _28, adder_1_out}));  // open: cin, cout
  Adder #(.width(32)) adder_2 (
    .a({_31, _30, _29, _28, adder_1_out}), .b(shifter_1_out), .out(adder_2_out));  // open: cin, cout
  and and_1 (and_1_out, nPC_sel, zero);
  Multiplexer #(.select(1), .width(32), .disabled("Z"), .enable("false")) multiplexer_1 (
    .in0({_31, _30, _29, _28, adder_1_out}), .in1(adder_2_out), .out(multiplexer_1_out), .sel(and_1_out));
  Multiplexer #(.select(1), .width(32), .disabled("Z"), .enable("false")) multiplexer_2 (
    .in0(multiplexer_1_out), .in1({_31, _30, _29, _28, ins[25:0], 2'b00}), .out(multiplexer_2_out), .sel(J));
  Register #(.width(32), .trigger("rising"), .Select("low")) pc (
    .D(multiplexer_2_out), .Q({pc_q_4, pc_q_3, pc_q[10], pc_q_2, pc_q[1:0]}), .clk(clk), .clr(reset));  // open: en
  ROM #(.addrWidth(8), .dataWidth(8), .Select("low")) rom_1 (.addr(pc_q_2), .data(ins[31:24]));
  ROM #(.addrWidth(8), .dataWidth(8), .Select("low")) rom_2 (.addr(pc_q_2), .data(ins[23:16]));
  ROM #(.addrWidth(8), .dataWidth(8), .Select("low")) rom_3 (.addr(pc_q_2), .data(ins[15:8]));
  ROM #(.addrWidth(8), .dataWidth(8), .Select("low")) rom_4 (.addr(pc_q_2), .data(ins[7:0]));
  // Probe on ins

  // Other names for the same wires on the sheet: imm[15:0] = ins[15:0];
  //   j_addr[31:2] = {_31, _30, _29, _28, ins[25:0]}

  // Notes on the sheet:
  //   contents of rom_1 (hex, n*v repeats v):
  //   34 34 0 0 1 ac 8c 11 3c 8 34 3c 8
  //   contents of rom_2 (hex, n*v repeats v):
  //   3 6 66 66 2a 9 a 2a b 10 b 9 10
  //   contents of rom_3 (hex, n*v repeats v):
  //   0 0 40 48 4*0 cd 0 ef 45
  //   contents of rom_4 (hex, n*v repeats v):
  //   93 ae 21 23 21 10 10 2 cd d ef 67 7
endmodule

module DM (
  input  in_1,
  input  in_2,
  input  in_3,
  input  [31:0] \地址 ,
  input  [31:0] \数据 ,
  output [31:0] \数据输出 
);

  RAM #(.addrWidth(8), .dataWidth(8), .bus("separate"), .Select("low")) ram_1 (
    .addr(\地址 [9:2]), .din(\数据 [7:0]), .data(\数据输出 [7:0]), .str(in_3), .clk(in_1), .clr(in_2));  // open: sel, ld
  RAM #(.addrWidth(8), .dataWidth(8), .bus("separate"), .Select("low")) ram_2 (
    .addr(\地址 [9:2]), .din(\数据 [15:8]), .data(\数据输出 [15:8]), .str(in_3), .clk(in_1), .clr(in_2));  // open: sel, ld
  RAM #(.addrWidth(8), .dataWidth(8), .bus("separate"), .Select("low")) ram_3 (
    .addr(\地址 [9:2]), .din(\数据 [23:16]), .data(\数据输出 [23:16]), .str(in_3), .clk(in_1), .clr(in_2));  // open: sel, ld
  RAM #(.addrWidth(8), .dataWidth(8), .bus("separate"), .Select("low")) ram_4 (
    .addr(\地址 [9:2]), .din(\数据 [31:24]), .data(\数据输出 [31:24]), .str(in_3), .clk(in_1), .clr(in_2));  // open: sel, ld

  // Other names for the same wires on the sheet: clk = in_1; MemWrite = in_3; reset = in_2
endmodule
